// Logisim project tp2.circ as structural Verilog: 6 circuits, main circuit q1p1
module q1p1 (
  input  A,
  input  B,
  output S
);

  wire nand_1_out, or_1_out;

  or or_1 (or_1_out, A, B);
  not nand_1 (nand_1_out, A);  // NAND_Gate
  and and_1 (S, or_1_out, nand_1_out);
endmodule

module q1p2 (
  input  A,
  input  B,
  output S
);

  wire not_1_out;

  not not_1 (not_1_out, B);
  nor nor_1 (S, not_1_out, A);
endmodule

module add1 (
  input  A,
  input  B,
  output S,
  output Rs
);

  xor xor_1 (S, A, B);
  and and_1 (Rs, A, B);
endmodule

module add1r (
  input  A,
  input  B,
  input  Re,
  output S,
  output Rs
);

  wire and_1_out, and_2_out, and_3_out, and_4_out, and_5_out, and_6_out, and_7_out, not_1_out, not_2_out,
       not_3_out, not_4_out, not_5_out, not_6_out;

  not not_1 (not_1_out, A);
  not not_2 (not_2_out, B);
  not not_3 (not_3_out, A);
  not not_4 (not_4_out, Re);
  not not_5 (not_5_out, B);
  not not_6 (not_6_out, Re);
  and and_1 (and_1_out, B, Re);
  and and_2 (and_2_out, A, Re);
  and and_3 (and_3_out, A, B);
  and and_4 (and_4_out, not_1_out, not_2_out, Re);
  and and_5 (and_5_out, not_3_out, B, not_4_out);
  and and_6 (and_6_out, A, not_5_out, not_6_out);
  and and_7 (and_7_out, A, B, Re);
  or or_1 (Rs, and_1_out, and_2_out, and_3_out);
  or or_2 (S, and_4_out, and_5_out, and_6_out, and_7_out);
endmodule

module add4 (
  input  [3:0] in_1,
  input  [3:0] in_2,
  output [3:0] out_3,
  output out_4
);

  wire add1_1_rs, add1r_simple_1_rs, add1r_simple_2_rs;

  add1 add1_1 (.A(in_1[0]), .B(in_2[0]), .S(out_3[0]), .Rs(add1_1_rs));
  add1r_simple add1r_simple_1 (.A(add1_1_rs), .B(in_1[1]), .Re(in_2[1]), .S(out_3[1]), .Rs(add1r_simple_1_rs));
  add1r_simple add1r_simple_2 (.A(add1r_simple_1_rs), .B(in_1[2]), .Re(in_2[2]), .S(out_3[2]), .Rs(add1r_simple_2_rs));
  add1r_simple add1r_simple_3 (.A(add1r_simple_2_rs), .B(in_1[3]), .Re(in_2[3]), .S(out_3[3]), .Rs(out_4));
endmodule

module add1r_simple (
  input  A,
  input  B,
  input  Re,
  output S,
  output Rs
);

  wire add1_1_rs, add1_1_s, add1_2_rs;

  add1 add1_1 (.A(B), .B(Re), .S(add1_1_s), .Rs(add1_1_rs));
  add1 add1_2 (.A(A), .B(add1_1_s), .S(S), .Rs(add1_2_rs));
  or or_1 (Rs, add1_2_rs, add1_1_rs);
endmodule
