// Logisim project tp3ex1.circ as structural Verilog: 5 circuits, main circuit S-R flipflop
module S_R_flipflop (
  input  in_1,
  input  in_2,
  input  in_3,
  output out_4
);

  S_R_Flip_Flop s_r_ff_1 (.S(in_1), .clk(in_2), .R(in_3), .Q(out_4));  // open: Qn, preset, reset, en
endmodule

module registre8bits (
  input  in_1,
  input  [7:0] in_2,
  output [7:0] out_3
);

  wire not_1_out, not_2_out, not_3_out, not_4_out, not_5_out, not_6_out, not_7_out, not_8_out;

  S_R_flipflop s_r_flipflop_1 (.in_1(in_2[0]), .in_2(in_1), .in_3(not_1_out), .out_4(out_3[0]));
  not not_1 (not_1_out, in_2[0]);
  S_R_flipflop s_r_flipflop_2 (.in_1(in_2[1]), .in_2(in_1), .in_3(not_2_out), .out_4(out_3[1]));
  not not_2 (not_2_out, in_2[1]);
  S_R_flipflop s_r_flipflop_3 (.in_1(in_2[2]), .in_2(in_1), .in_3(not_3_out), .out_4(out_3[2]));
  not not_3 (not_3_out, in_2[2]);
  S_R_flipflop s_r_flipflop_4 (.in_1(in_2[3]), .in_2(in_1), .in_3(not_4_out), .out_4(out_3[3]));
  not not_4 (not_4_out, in_2[3]);
  S_R_flipflop s_r_flipflop_5 (.in_1(in_2[4]), .in_2(in_1), .in_3(not_5_out), .out_4(out_3[4]));
  not not_5 (not_5_out, in_2[4]);
  S_R_flipflop s_r_flipflop_6 (.in_1(in_2[5]), .in_2(in_1), .in_3(not_6_out), .out_4(out_3[5]));
  not not_6 (not_6_out, in_2[5]);
  S_R_flipflop s_r_flipflop_7 (.in_1(in_2[6]), .in_2(in_1), .in_3(not_7_out), .out_4(out_3[6]));
  not not_7 (not_7_out, in_2[6]);
  S_R_flipflop s_r_flipflop_8 (.in_1(in_2[7]), .in_2(in_1), .in_3(not_8_out), .out_4(out_3[7]));
  not not_8 (not_8_out, in_2[7]);
endmodule

module add8 (
  input  in_1,
  input  [7:0] in_2,
  input  [7:0] in_3,
  input  in_4,
  input  [7:0] b,
  output [7:0] out_6,
  output out_7
);

  wire [7:0] multiplexer_1_out, registre8bits_1_out_3;

  registre8bits registre8bits_1 (.out_3(registre8bits_1_out_3), .in_1(in_4), .in_2(in_3));
  Multiplexer #(.width(8), .enable("false")) multiplexer_1 (
    .in0(in_2), .in1(registre8bits_1_out_3), .out(multiplexer_1_out), .sel(in_1));
  Adder adder_1 (.a(multiplexer_1_out), .b(b), .out(out_6), .cout(out_7));  // open: cin

  // Notes on the sheet:
  //   a
endmodule

module C2sur8bits (
  input  [7:0] in_1,
  input  [7:0] in_2,
  output [7:0] out_3
);

  wire [7:0] not_1_out;

  assign not_1_out = ~in_1;  // NOT_Gate not_1, 8 bits wide
  Adder adder_1 (.a(not_1_out), .b(in_2), .out(out_3));  // open: cin, cout
endmodule

module add_sous8bits (
  input  SEL,
  input  [7:0] in_2,
  input  [7:0] in_3,
  input  in_4,
  input  soustraction,
  input  [7:0] b,
  output [7:0] out_7
);

  wire [7:0] adder_1_out, multiplexer_1_out, registre8bits_1_out_3, subtractor_1_out;

  registre8bits registre8bits_1 (.out_3(registre8bits_1_out_3), .in_1(in_4), .in_2(in_3));
  Multiplexer #(.width(8), .enable("false")) multiplexer_1 (
    .in0(in_2), .in1(registre8bits_1_out_3), .out(multiplexer_1_out), .sel(SEL));
  Adder adder_1 (.a(multiplexer_1_out), .b(b), .out(adder_1_out));  // open: cin, cout
  Subtractor subtractor_1 (.a(multiplexer_1_out), .b(b), .out(subtractor_1_out));  // open: bin, bout
  Multiplexer #(.width(8), .enable("false")) multiplexer_2 (
    .in0(adder_1_out), .in1(subtractor_1_out), .out(out_7), .sel(soustraction));

  // Notes on the sheet:
  //   a
endmodule
